# Fritzing sketch schéma station météo (saved by Fritzing 0.9.3b)

parts:
  U1 = ESP8266 NodeMCU LoLin module
  Composant1 = Barometric Pressure Sensor - BMP180 Breakout (GY-68)
  Composant2 = Humidity Sensor - HIH-4030 Breakout

nets:
  N1: U1.D1, Composant1.SCL
  N2: U1.D2, Composant1.SDA
  N3: U1.D4, Composant2.OUT
  3V3: U1.3V3, Composant1.VCC
  GND: U1.GND, Composant1.GND

custom parts:
  ESP8266 NodeMCU LoLin module: ESP8266 based NodeMCU
